// Logisim project A_84-2-1_to_5421_code_converter.circ as structural Verilog: 1 circuit, main circuit main
module main (
  input  W,
  input  X,
  input  Y,
  input  Z,
  output A___W,
  output B___X_W_Y_prime_Z_prime,
  output out_7,
  output out_8
);

  wire and_1_out, and_2_out, and_3_out, and_4_out, and_5_out, and_6_out, and_8_out, not_1_out, not_2_out,
       not_3_out, not_4_out, or_1_out, or_3_out;

  not not_1 (not_1_out, W);
  not not_2 (not_2_out, X);
  not not_3 (not_3_out, Y);
  not not_4 (not_4_out, Z);
  or or_1 (or_1_out, W, and_1_out);
  and and_1 (and_1_out, not_3_out, not_4_out);
  and and_2 (and_2_out, W, not_3_out);
  and and_3 (and_3_out, not_3_out, Z);
  and and_4 (and_4_out, not_1_out, Y);
  and and_5 (and_5_out, not_1_out, Z);
  and and_6 (and_6_out, W, not_4_out);
  and and_7 (B___X_W_Y_prime_Z_prime, X, or_1_out);
  and and_8 (and_8_out, and_4_out, not_4_out);
  or or_2 (out_8, and_5_out, and_6_out);
  or or_3 (or_3_out, and_3_out, and_8_out);
  or or_4 (out_7, and_2_out, or_3_out);

  assign A___W = W;

  // Notes on the sheet:
  //   D = W'Z + WZ'
  //   C = WY'+Y'Z+W'YZ'
  //   OM VAGHELA(25BCE533)   PRACTICAL 3
endmodule
