// Logisim project All_Gates_Using_Nand_Universal_Gates.circ as structural Verilog: 1 circuit, main circuit main
module main (
  input  in_1,
  input  in_2,
  input  in_3,
  input  in_4,
  input  in_5,
  input  in_6,
  input  in_7,
  input  in_8,
  input  in_9,
  output out_10,
  output out_11,
  output out_12,
  output out_13,
  output out_14
);

  wire nand_2_out, nand_3_out, nand_4_out, nand_5_out, nand_6_out, nand_9_out, nand_10_out, nand_12_out,
       nand_13_out, nand_14_out;

  nand nand_1 (out_11, in_2, in_2);
  nand nand_2 (nand_2_out, in_7, in_9);
  nand nand_3 (nand_3_out, in_7, nand_2_out);
  nand nand_4 (nand_4_out, nand_2_out, in_9);
  nand nand_5 (nand_5_out, in_4, in_4);
  nand nand_6 (nand_6_out, in_5, in_5);
  nand nand_7 (out_14, nand_3_out, nand_4_out);
  nand nand_8 (out_12, nand_5_out, nand_6_out);
  nand nand_9 (nand_9_out, in_1, in_3);
  nand nand_10 (nand_10_out, in_6, in_8);
  nand nand_11 (out_10, nand_9_out, nand_9_out);
  nand nand_12 (nand_12_out, in_6, nand_10_out);
  nand nand_13 (nand_13_out, nand_10_out, in_8);
  nand nand_14 (nand_14_out, nand_12_out, nand_13_out);
  nand nand_15 (out_13, nand_14_out, nand_14_out);

  // Notes on the sheet:
  //   NOT GATE
  //   X-OR
  //   OR GATE
  //   OM VAGHELA(25BCE533) PRACTICAL - 1
  //   AND GATE
  //   X-NOR
endmodule
