// Logisim project All_Gates_Using_Nor_Universal_Gates.circ as structural Verilog: 1 circuit, main circuit main
module main (
  input  in_1,
  input  in_2,
  input  in_3,
  input  in_4,
  input  in_5,
  input  in_6,
  input  in_7,
  input  in_8,
  input  in_9,
  output out_10,
  output out_11,
  output out_12,
  output out_13,
  output out_14
);

  wire nor_2_out, nor_3_out, nor_5_out, nor_6_out, nor_7_out, nor_8_out, nor_9_out, nor_12_out, nor_13_out,
       nor_14_out;

  nor nor_1 (out_10, in_2, in_2);
  nor nor_2 (nor_2_out, in_5, in_5);
  nor nor_3 (nor_3_out, in_6, in_6);
  nor nor_4 (out_13, nor_2_out, nor_3_out);
  nor nor_5 (nor_5_out, in_8, in_9);
  nor nor_6 (nor_6_out, in_8, nor_5_out);
  nor nor_7 (nor_7_out, nor_5_out, in_9);
  nor nor_8 (nor_8_out, in_1, in_3);
  nor nor_9 (nor_9_out, nor_6_out, nor_7_out);
  nor nor_10 (out_11, nor_8_out, nor_8_out);
  nor nor_11 (out_14, nor_9_out, nor_9_out);
  nor nor_12 (nor_12_out, in_4, in_7);
  nor nor_13 (nor_13_out, in_4, nor_12_out);
  nor nor_14 (nor_14_out, nor_12_out, in_7);
  nor nor_15 (out_12, nor_13_out, nor_14_out);

  // Notes on the sheet:
  //   NOT GATE
  //   AND GATE
  //   OM VAGHELA(25BCE533) PRACTICAL - 1
  //   XOR GATE
  //   OR GATE
  //   XNOR GATE
endmodule
