// Logisim project BCD-To-2421-code-converter.circ as structural Verilog: 1 circuit, main circuit main
module main (
  input  W,
  input  in_2,
  input  in_3,
  input  Z,
  output A___W_XZ_XY,
  output B___W_XY_XZ_prime,
  output C__W_XY_prime_Z_X_prime_Y,
  output D__Z
);

  wire and_1_out, and_2_out, and_3_out, and_4_out, and_5_out, and_6_out, not_1_out, not_2_out, not_3_out,
       or_1_out, or_2_out, or_4_out;

  not not_1 (not_1_out, in_2);
  not not_2 (not_2_out, in_3);
  not not_3 (not_3_out, Z);
  and and_1 (and_1_out, in_2, Z);
  and and_2 (and_2_out, in_2, in_3);
  and and_3 (and_3_out, in_2, not_3_out);
  and and_4 (and_4_out, not_1_out, in_3);
  and and_5 (and_5_out, in_2, not_2_out);
  or or_1 (or_1_out, W, and_1_out);
  or or_2 (or_2_out, and_2_out, W);
  and and_6 (and_6_out, and_5_out, Z);
  or or_3 (B___W_XY_XZ_prime, or_2_out, and_3_out);
  or or_4 (or_4_out, and_6_out, W);
  or or_5 (A___W_XZ_XY, or_1_out, and_2_out);
  or or_6 (C__W_XY_prime_Z_X_prime_Y, and_4_out, or_4_out);

  assign D__Z = Z;

  // Notes on the sheet:
  //   X
  //   Y
  //   OM VAGHELA(25BCE533)   PRACTICAL 3
  //   XZ
  //   XY
  //   XZ'
  //   X'Y
  //   XY'
  //   XY'Z
endmodule
