// Logisim project BCD_adder_Circuit.circ as structural Verilog: 1 circuit, main circuit main
module main (
  input  [3:0] in_1,
  input  [3:0] in_2,
  input  in_3,
  input  in_4,
  output out_5,
  output [3:0] out_6
);

  wire adder_1_cout, and_1_out, and_2_out;
  wire [3:0] adder_1_out;

  or or_1 (out_5, adder_1_cout, and_1_out, and_2_out);
  and and_1 (and_1_out, adder_1_out[3], adder_1_out[2]);
  and and_2 (and_2_out, adder_1_out[3], adder_1_out[1]);
  Adder #(.width(4)) adder_1 (.a(in_1), .b(in_2), .out(adder_1_out), .cout(adder_1_cout));  // open: cin
  Adder #(.width(4)) adder_2 (.a(adder_1_out), .b({in_3, {2{out_5}}, in_4}), .out(out_6));  // open: cin, cout

  // Notes on the sheet:
  //   OM VAGHELA(25BCE533)   PRACTICAL 4
endmodule
