// Logisim project BINTOGRAY_VICEV.circ as structural Verilog: 1 circuit, main circuit main
module main (
  input  in_1,
  input  in_2,
  input  in_3,
  input  in_4,
  input  in_5,
  input  in_6,
  input  in_7,
  input  in_8,
  output out_9,
  output out_10,
  output out_11,
  output out_12,
  output out_13,
  output out_14,
  output out_15,
  output out_16
);

  xor xor_1 (out_12, in_2, in_4);
  xor xor_2 (out_14, in_4, in_6);
  xor xor_3 (out_16, in_6, in_8);
  xor xor_4 (out_11, in_1, in_3);
  xor xor_5 (out_13, out_11, in_5);
  xor xor_6 (out_15, out_13, in_7);

  assign out_9 = in_1;
  assign out_10 = in_2;

  // Notes on the sheet:
  //   BINARY TO GRAY
  //   GRAY TO BINARY
endmodule
