// Logisim project Basic_logic_gates.circ as structural Verilog: 1 circuit, main circuit main
module main (
  input  in_1,
  input  in_2,
  input  in_3,
  input  in_4,
  input  in_5,
  input  in_6,
  input  in_7,
  input  in_8,
  input  in_9,
  input  in_10,
  input  in_11,
  input  in_12,
  input  in_13,
  output out_14,
  output out_15,
  output out_16,
  output out_17,
  output out_18,
  output out_19,
  output out_20
);

  and and_1 (out_14, in_1, in_3);
  or or_1 (out_16, in_5, in_6);
  not not_1 (out_18, in_9);
  nand nand_1 (out_19, in_10, in_11);
  nor nor_1 (out_20, in_12, in_13);
  xor xor_1 (out_15, in_2, in_4);
  xnor xnor_1 (out_17, in_7, in_8);

  // Notes on the sheet:
  //   AND GATE
  //   OR GATE
  //   NOT GATE
  //   NAND GATE
  //   NOR GATE
  //   OM VAGHELA(25BCE533) PRACTICAL - 1
  //   XOR GATE
  //   XNOR GATE
endmodule
