// Logisim project Elevetor_Circuit_Implementation.circ as structural Verilog: 3 circuits, main circuit main
module main (
  input  Gnd,
  input  Floor_1,
  input  Floor_2,
  input  Door_open_Stop,
  input  Floor_3,
  output Going_Down,
  output Reached,
  output Going_Up
);

  wire CLOCK_out, n7_segment_1_out_5, n7_segment_1_out_6, n7_segment_1_out_7, n7_segment_1_out_8,
       n7_segment_1_out_9, n7_segment_1_out_10, n7_segment_1_out_11;
  wire [1:0] floor_traversal_1_out_4, priority_encoder_1_out;

  Priority_Encoder #(.select(2)) priority_encoder_1 (
    .in0(Gnd), .in1(Floor_1), .in2(Floor_2), .in3(Floor_3), .out(priority_encoder_1_out));  // open: gs, en_out, en_in
  Clock CLOCK (.out(CLOCK_out));
  floor_traversal floor_traversal_1 (
    .in_1(priority_encoder_1_out), .in_2(Door_open_Stop), .in_3(CLOCK_out), .out_4(floor_traversal_1_out_4));
  _7_segment u_7_segment_1 (
    .W(1'b0), .X(1'b0), .Y(floor_traversal_1_out_4[1]), .Z(floor_traversal_1_out_4[0]),
    .out_5(n7_segment_1_out_5), .out_6(n7_segment_1_out_6), .out_7(n7_segment_1_out_7),
    .out_8(n7_segment_1_out_8), .out_9(n7_segment_1_out_9), .out_10(n7_segment_1_out_10),
    .out_11(n7_segment_1_out_11));
  Comparator #(.width(2), .mode("unsigned")) comparator_1 (
    .a(floor_traversal_1_out_4), .b(priority_encoder_1_out), .gt(Going_Down), .eq(Reached), .lt(Going_Up));
  _7_Segment_Display u_7_segment_display_1 (
    .g(n7_segment_1_out_11), .f(n7_segment_1_out_5), .a(n7_segment_1_out_6), .b(n7_segment_1_out_7),
    .e(n7_segment_1_out_10), .d(n7_segment_1_out_9), .c(n7_segment_1_out_8));  // open: dp
endmodule

module floor_traversal (
  input  [1:0] in_1,
  input  in_2,
  input  in_3,
  output [1:0] out_4
);

  wire and_1_out, and_2_out, and_3_out, not_1_out, not_2_out, not_3_out, not_4_out, or_1_out, or_2_out,
       xor_1_out;

  not not_1 (not_1_out, in_2);
  xor xor_1 (xor_1_out, in_1[1], out_4[1]);
  not not_2 (not_2_out, in_1[0]);
  and and_1 (and_1_out, not_1_out, in_3);
  and and_2 (and_2_out, out_4[0], in_1[1]);
  not not_3 (not_3_out, out_4[0]);
  and and_3 (and_3_out, not_3_out, not_4_out);
  not not_4 (not_4_out, in_1[1]);
  or or_1 (or_1_out, in_1[0], xor_1_out);
  or or_2 (or_2_out, not_2_out, xor_1_out);
  J_K_Flip_Flop j_k_ff_1 (.J(and_2_out), .clk(and_1_out), .K(and_3_out), .Q(out_4[1]));  // open: Qn, preset, en, reset
  J_K_Flip_Flop j_k_ff_2 (.J(or_1_out), .clk(and_1_out), .K(or_2_out), .Q(out_4[0]));  // open: Qn, preset, en, reset

  // Notes on the sheet:
  //   Working Circuit
endmodule

module _7_segment (
  input  W,
  input  X,
  input  Y,
  input  Z,
  output out_5,
  output out_6,
  output out_7,
  output out_8,
  output out_9,
  output out_10,
  output out_11
);

  wire and_1_out, and_2_out, and_3_out, and_4_out, and_5_out, and_6_out, and_7_out, and_8_out, and_9_out,
       not_1_out, not_2_out, not_3_out, or_1_out, xnor_1_out, xnor_2_out, xor_1_out;

  not not_1 (not_1_out, X);
  not not_2 (not_2_out, Y);
  not not_3 (not_3_out, Z);
  or or_1 (or_1_out, not_3_out, not_2_out);
  and and_1 (and_1_out, not_3_out, not_2_out);
  xnor xnor_1 (xnor_1_out, X, Z);
  xnor xnor_2 (xnor_2_out, Y, Z);
  and and_2 (and_2_out, X, or_1_out);
  and and_3 (and_3_out, not_1_out, not_3_out);
  and and_4 (and_4_out, X, not_2_out, Z);
  and and_5 (and_5_out, not_1_out, Y);
  and and_6 (and_6_out, Y, not_3_out);
  and and_7 (and_7_out, Y, not_3_out);
  and and_8 (and_8_out, not_1_out, not_3_out);
  xor xor_1 (xor_1_out, X, Y);
  and and_9 (and_9_out, Y, not_3_out);
  or or_2 (out_5, W, and_2_out, and_1_out);
  or or_3 (out_6, W, Y, xnor_1_out);
  or or_4 (out_7, xnor_2_out, not_1_out);
  or or_5 (out_8, X, not_2_out, Z);
  or or_6 (out_9, W, and_3_out, and_4_out, and_5_out, and_6_out);
  or or_7 (out_10, and_7_out, and_8_out);
  or or_8 (out_11, xor_1_out, and_9_out, W);

  // Notes on the sheet:
  //   BCD TO 7 SEGMENT DISPLAY
endmodule
