// Logisim project Excess_3_adder_circuit.circ as structural Verilog: 1 circuit, main circuit main
module main (
  input  [3:0] in_1,
  input  [3:0] in_2,
  input  in_3,
  output _0_0,
  output [3:0] out_5
);

  wire [3:0] adder_1_out;
  wire [3:3] not_1_out;

  not not_1 (not_1_out[3], _0_0);
  Adder #(.width(4)) adder_1 (.a(in_1), .b(in_2), .out(adder_1_out), .cout(_0_0));  // open: cin
  Adder #(.width(4)) adder_2 (.a(adder_1_out), .b({{2{not_1_out[3]}}, _0_0, in_3}), .out(out_5));  // open: cin, cout

  // Notes on the sheet:
  //   OM VAGHELA(25BCE533)   PRACTICAL 4
endmodule
