// Logisim project Gray_to_Binary-Binary_to_Gray.circ as structural Verilog: 1 circuit, main circuit main
module main (
  input  G1,
  input  B1,
  input  G2,
  input  B2,
  input  G3,
  input  B3,
  input  G4,
  input  B4,
  output B1_2,
  output G1_2,
  output B2_2,
  output G2_2,
  output B3_2,
  output G3_2,
  output B4_2,
  output G4_2
);

  xor xor_1 (G2_2, B1, B2);
  xor xor_2 (G3_2, B2, B3);
  xor xor_3 (G4_2, B3, B4);
  xor xor_4 (B2_2, G1, G2);
  xor xor_5 (B3_2, B2_2, G3);
  xor xor_6 (B4_2, B3_2, G4);

  assign B1_2 = G1;
  assign G1_2 = B1;

  // Notes on the sheet:
  //   BINARY TO GRAY
  //   OM VAGHELA(25BCE533) PRACTICAL - 2
  //   GRAY TO BINARY
endmodule
