// Logisim project Half_Subtractor_Full_Subtractor.circ as structural Verilog: 1 circuit, main circuit main
module main (
  input  in_1,
  input  in_2,
  input  C,
  input  B,
  input  A,
  output out_6,
  output out_7,
  output DIFFERENCE,
  output out_9
);

  wire and_2_out, and_3_out, not_1_out, not_2_out, xor_2_out;

  not not_1 (not_1_out, in_1);
  and and_1 (out_6, not_1_out, in_2);
  xor xor_1 (DIFFERENCE, in_1, in_2);
  and and_2 (and_2_out, B, C);
  xor xor_2 (xor_2_out, C, B);
  not not_2 (not_2_out, A);
  and and_3 (and_3_out, xor_2_out, not_2_out);
  xor xor_3 (out_9, xor_2_out, A);
  or or_1 (out_7, and_2_out, and_3_out);

  // Notes on the sheet:
  //   HALF SUBTRACTOR
  //   BORROW
  //   OM VAGHELA(25BCE533)   PRACTICAL 2
  //   FULL SUBTRACTOR
  //   DIFFERENCE
  //   BORROW
endmodule
