// Logisim project Half_and_full_Adder_circuit.circ as structural Verilog: 1 circuit, main circuit main
module main (
  input  A,
  input  in_2,
  input  B,
  input  in_4,
  input  C,
  output SUM,
  output SUM_2,
  output CARRY,
  output CARRY_2
);

  wire and_2_out, and_3_out, xor_2_out;

  and and_1 (CARRY, in_2, in_4);
  xor xor_1 (SUM, in_2, in_4);
  xor xor_2 (xor_2_out, A, B);
  xor xor_3 (SUM_2, xor_2_out, C);
  and and_2 (and_2_out, xor_2_out, C);
  and and_3 (and_3_out, A, B);
  or or_1 (CARRY_2, and_2_out, and_3_out);

  // Notes on the sheet:
  //   HALF ADDER
  //   OM VAGHELA(25BCE533) PRACTICAL - 2
  //   FULL ADDER
endmodule
