// Logisim project Mod_15_Asynchronous_counter.circ as structural Verilog: 1 circuit, main circuit main
module main (
  output A1,
  output A2,
  output A3,
  output A4
);

  wire clock_1_out, not_1_out, not_2_out, not_3_out, not_4_out;

  Clock clock_1 (.out(clock_1_out));
  not not_1 (not_1_out, clock_1_out);
  J_K_Flip_Flop j_k_ff_1 (.J(1'b1), .clk(not_1_out), .K(1'b1), .Q(A1));  // open: Qn, preset, en, reset
  not not_2 (not_2_out, A1);
  J_K_Flip_Flop j_k_ff_2 (.J(1'b1), .clk(not_2_out), .K(1'b1), .Q(A2));  // open: Qn, preset, en, reset
  not not_3 (not_3_out, A2);
  J_K_Flip_Flop j_k_ff_3 (.J(1'b1), .clk(not_3_out), .K(1'b1), .Q(A3));  // open: Qn, preset, en, reset
  not not_4 (not_4_out, A3);
  J_K_Flip_Flop j_k_ff_4 (.J(1'b1), .clk(not_4_out), .K(1'b1), .Q(A4));  // open: Qn, preset, en, reset
endmodule
