// Logisim project Mod_9_Synchronous_Counter.circ as structural Verilog: 1 circuit, main circuit main
module main (
  output A,
  output B,
  output C,
  output D
);

  wire and_1_out, and_2_out, clock_1_out, not_1_out, or_1_out;

  Clock clock_1 (.out(clock_1_out));
  not not_1 (not_1_out, A);
  T_Flip_Flop t_ff_1 (.clk(clock_1_out), .T(or_1_out), .Q(A));  // open: Qn, preset, reset, en
  T_Flip_Flop t_ff_2 (.clk(clock_1_out), .T(and_2_out), .Q(B));  // open: Qn, preset, reset, en
  T_Flip_Flop t_ff_3 (.clk(clock_1_out), .T(D), .Q(C));  // open: Qn, preset, reset, en
  T_Flip_Flop t_ff_4 (.clk(clock_1_out), .T(not_1_out), .Q(D));  // open: Qn, preset, reset, en
  and and_1 (and_1_out, B, C, D);
  or or_1 (or_1_out, A, and_1_out);
  and and_2 (and_2_out, C, D);
endmodule
