// Logisim project Mod_9_ripple_Asynchronous_Counter.circ as structural Verilog: 1 circuit, main circuit main
module main (
  output Q1,
  output Q2,
  output Q4,
  output Q8
);

  wire and_1_out, clock_1_out, j_k_ff_4_qn, not_1_out, not_2_out, not_3_out, not_4_out;

  Clock clock_1 (.out(clock_1_out));
  not not_1 (not_1_out, clock_1_out);
  not not_2 (not_2_out, Q1);
  not not_3 (not_3_out, Q2);
  not not_4 (not_4_out, Q1);
  J_K_Flip_Flop j_k_ff_1 (.J(1'b1), .clk(not_1_out), .K(1'b1), .Q(Q1));  // open: Qn, preset, en, reset
  J_K_Flip_Flop j_k_ff_2 (.J(j_k_ff_4_qn), .clk(not_2_out), .K(1'b1), .Q(Q2));  // open: Qn, preset, en, reset
  J_K_Flip_Flop j_k_ff_3 (.J(1'b1), .clk(not_3_out), .K(1'b1), .Q(Q4));  // open: Qn, preset, en, reset
  J_K_Flip_Flop j_k_ff_4 (
    .J(and_1_out), .clk(not_4_out), .K(1'b1), .Q(Q8), .Qn(j_k_ff_4_qn));  // open: preset, en, reset
  and and_1 (and_1_out, Q4, Q2);
endmodule
