// Logisim project Multiplexer_implementation.circ as structural Verilog: 1 circuit, main circuit main
module main (
  input  in_1,
  input  in_2,
  input  A,
  input  [3:0] in_4,
  input  A_2,
  input  C,
  input  in_7,
  input  [2:0] in_8,
  output out_9,
  output out_10
);

  wire and_1_out, and_2_out, not_1_out, not_2_out, not_3_out, or_1_out;

  not not_1 (not_1_out, A);
  Multiplexer #(.select(4)) multiplexer_1 (
    .in0(in_1), .in1(in_1), .in2(in_1), .in3(not_1_out), .in4(in_1), .in5(in_1), .in6(in_1), .in7(in_1),
    .in8(A), .in9(in_1), .in10(in_2), .in11(in_2), .in12(A), .in13(in_1), .in14(A), .in15(in_1), .out(out_9),
    .sel(in_4));  // open: en
  not not_2 (not_2_out, A_2);
  not not_3 (not_3_out, C);
  and and_1 (and_1_out, not_2_out, not_3_out);
  and and_2 (and_2_out, A_2, C);
  or or_1 (or_1_out, not_3_out, and_2_out);
  Multiplexer #(.select(3)) multiplexer_2 (
    .in0(in_7), .in1(in_7), .in2(in_7), .in3(and_1_out), .in4(A_2), .in5(C), .in6(or_1_out), .in7(not_3_out),
    .out(out_10), .sel(in_8));  // open: en

  // Notes on the sheet:
  //   Tacking A and C as selection Line
  //   OM VAGHELA(25BCE533)   PRACTICAL 5
  //   F(A,B,C,D,E) = ABE' + BC'D + A'C'DE
endmodule
