// Logisim project Parity_generator_and_checker.circ as structural Verilog: 1 circuit, main circuit main
module main (
  input  A,
  input  B,
  input  C,
  output ODD_parity,
  output out_5
);

  wire xor_1_out, xor_2_out, xor_3_out;

  xor xor_1 (xor_1_out, A, B);
  xor xor_2 (xor_2_out, A, B);
  xor xor_3 (xor_3_out, C, ODD_parity);
  xnor xnor_1 (ODD_parity, xor_1_out, C);
  xnor xnor_2 (out_5, xor_2_out, xor_3_out);

  // Notes on the sheet:
  //   OM VAGHELA(25BCE533)   PRACTICAL 3
endmodule
