// Logisim project RS_JK__FlipFlop.circ as structural Verilog: 1 circuit, main circuit main
module main (
  input  R,
  input  R_2,
  input  S,
  input  S_2,
  input  R_3,
  input  in_6,
  input  S_3,
  input  J,
  output Q,
  output Q_2,
  output Q_prime,
  output Q_prime_2,
  output Q_3,
  output Q_4,
  output Q_prime_3,
  output Q_prime_4
);

  wire and_1_out, and_2_out, and_3_out, and_4_out, clock_1_out, clock_2_out;

  Clock clock_1 (.out(clock_1_out));
  and and_1 (and_1_out, R_3, clock_1_out);
  and and_2 (and_2_out, clock_1_out, S_3);
  nor nor_1 (Q, R, Q_prime);
  nor nor_2 (Q_prime, Q, S);
  nor nor_3 (Q_3, and_1_out, Q_prime_3);
  nor nor_4 (Q_prime_3, Q_3, and_2_out);
  Clock clock_2 (.out(clock_2_out));
  and and_3 (and_3_out, Q_4, in_6, clock_2_out);
  and and_4 (and_4_out, clock_2_out, J, Q_prime_4);
  nand nand_1 (Q_2, R_2, Q_prime_2);
  nand nand_2 (Q_prime_2, Q_2, S_2);
  nor nor_5 (Q_4, and_3_out, Q_prime_4);
  nor nor_6 (Q_prime_4, Q_4, and_4_out);

  // Notes on the sheet:
  //   NOR FF
  //   NOR WITH CLK FF
  //   K
  //   NAND FF
  //   JK FF
endmodule
