// Logisim project Seven_segment_display.circ as structural Verilog: 1 circuit, main circuit main
module main (
  input  W,
  input  X,
  input  Y,
  input  Z,
  output out_5,
  output out_6,
  output out_7,
  output out_8,
  output out_9,
  output out_10,
  output out_11
);

  wire and_1_out, and_2_out, and_3_out, and_4_out, and_5_out, and_6_out, and_7_out, and_8_out, and_9_out,
       not_1_out, not_2_out, not_3_out, or_1_out, xnor_1_out, xnor_2_out, xor_1_out;

  not not_1 (not_1_out, X);
  not not_2 (not_2_out, Y);
  not not_3 (not_3_out, Z);
  or or_1 (or_1_out, not_3_out, not_2_out);
  and and_1 (and_1_out, not_3_out, not_2_out);
  xnor xnor_1 (xnor_1_out, X, Z);
  xnor xnor_2 (xnor_2_out, Y, Z);
  and and_2 (and_2_out, X, or_1_out);
  and and_3 (and_3_out, not_1_out, not_3_out);
  and and_4 (and_4_out, X, not_2_out, Z);
  and and_5 (and_5_out, not_1_out, Y);
  and and_6 (and_6_out, Y, not_3_out);
  and and_7 (and_7_out, Y, not_3_out);
  and and_8 (and_8_out, not_1_out, not_3_out);
  xor xor_1 (xor_1_out, X, Y);
  and and_9 (and_9_out, Y, not_3_out);
  or or_2 (out_5, W, and_2_out, and_1_out);
  or or_3 (out_6, W, Y, xnor_1_out);
  or or_4 (out_7, xnor_2_out, not_1_out);
  or or_5 (out_8, X, not_2_out, Z);
  or or_6 (out_9, W, and_3_out, and_4_out, and_5_out, and_6_out);
  or or_7 (out_10, and_7_out, and_8_out);
  or or_8 (out_11, xor_1_out, and_9_out, W);

  // Notes on the sheet:
  //   BCD TO 7 SEGMENT DISPLAY
endmodule
