// Logisim project Shift_Register_Circuit.circ as structural Verilog: 1 circuit, main circuit main
module main (
  input  SL,
  input  I1,
  input  I2,
  input  I3,
  input  SR,
  input  I4,
  input  [1:0] in_7,
  output A1,
  output A2,
  output A3,
  output A4
);

  wire clock_1_out, multiplexer_1_out, multiplexer_2_out, multiplexer_3_out, multiplexer_4_out;

  Multiplexer #(.select(2)) multiplexer_1 (
    .in0(A1), .in1(SL), .in2(A2), .in3(I1), .out(multiplexer_1_out), .sel(in_7));  // open: en
  Multiplexer #(.select(2)) multiplexer_2 (
    .in0(A2), .in1(A1), .in2(A3), .in3(I2), .out(multiplexer_2_out), .sel(in_7));  // open: en
  Multiplexer #(.select(2)) multiplexer_3 (
    .in0(A3), .in1(A2), .in2(A4), .in3(I3), .out(multiplexer_3_out), .sel(in_7));  // open: en
  Multiplexer #(.select(2)) multiplexer_4 (
    .in0(A4), .in1(A3), .in2(SR), .in3(I4), .out(multiplexer_4_out), .sel(in_7));  // open: en
  Clock clock_1 (.out(clock_1_out));
  D_Flip_Flop d_ff_1 (.clk(clock_1_out), .D(multiplexer_1_out), .Q(A1));  // open: Qn, preset, en, reset
  D_Flip_Flop d_ff_2 (.clk(clock_1_out), .D(multiplexer_2_out), .Q(A2));  // open: Qn, preset, en, reset
  D_Flip_Flop d_ff_3 (.clk(clock_1_out), .D(multiplexer_3_out), .Q(A3));  // open: Qn, preset, en, reset
  D_Flip_Flop d_ff_4 (.clk(clock_1_out), .D(multiplexer_4_out), .Q(A4));  // open: Qn, preset, en, reset
endmodule
