// Logisim project T_Flipflop_and_D_Flipflop.circ as structural Verilog: 1 circuit, main circuit main
module main (
  input  T,
  input  in_2,
  output Q,
  output Q_prime,
  output out_5,
  output out_6
);

  wire and_1_out, and_2_out, clock_1_out, clock_2_out, nand_1_out, nand_2_out, nand_3_out;

  Clock clock_1 (.out(clock_1_out));
  and and_1 (and_1_out, Q, T, clock_1_out);
  and and_2 (and_2_out, clock_1_out, T, Q_prime);
  nor nor_1 (Q, and_1_out, Q_prime);
  nor nor_2 (Q_prime, Q, and_2_out);
  nand nand_1 (nand_1_out, in_2, in_2);
  Clock clock_2 (.out(clock_2_out));
  nand nand_2 (nand_2_out, in_2, clock_2_out);
  nand nand_3 (nand_3_out, clock_2_out, nand_1_out);
  nand nand_4 (out_5, nand_2_out, out_6);
  nand nand_5 (out_6, out_5, nand_3_out);

  // Notes on the sheet:
  //   T FF
  //   D FF
endmodule
