// Logisim project Three_bit_square_generator.circ as structural Verilog: 1 circuit, main circuit main
module main (
  input  X,
  input  Y,
  input  Z,
  input  in_4,
  output A_XY,
  output B_X_Y_prime___Z,
  output C_Z_XY_prime___X_prime_Y,
  output D__YZ_prime,
  output F___Z,
  output E___0
);

  wire not_1_out, not_2_out, not_3_out, or_1_out, xor_1_out;

  not not_1 (not_1_out, X);
  not not_2 (not_2_out, Y);
  not not_3 (not_3_out, Z);
  and and_1 (A_XY, X, Y);
  or or_1 (or_1_out, not_2_out, Z);
  xor xor_1 (xor_1_out, X, Y);
  and and_2 (D__YZ_prime, not_3_out, Y);
  and and_3 (B_X_Y_prime___Z, or_1_out, X);
  and and_4 (C_Z_XY_prime___X_prime_Y, xor_1_out, Z);

  assign E___0 = in_4;
  assign F___Z = Z;

  // Notes on the sheet:
  //   OM VAGHELA(25BCE533)   PRACTICAL 3
endmodule
